# Fritzing sketch FPGA Based SAFEHOUSE (saved by Fritzing 0.9.3b)

parts:
  4x4_Matrix_Keypad = KEYPAD 4x4
  S2 = Pushbutton [package="[THT]"]
  S3 = Pushbutton [package="[THT]"]
  R1 = Resistor [tolerance=±5% resistance=1k package=THT]
  R2 = Resistor [tolerance=±5% resistance=1k package=THT]
  Safehouse_SoC = IC, DIP package, 32 pins [chip_label=IC1]
  PIR1 = PIR sensor
  Flame_Sensor = KY-026
  Gas_Sensor = GAS_SENSOR [package=mq-3]
  LED2 = smd LED [color="Red (660nm)" package="0603 [SMD]"]
  LED3 = smd LED [color="Red (660nm)" package="0603 [SMD]"]
  LEDs = smd LED [color="Red (660nm)" package="0603 [SMD]"]
  LED5 = smd LED [color="Red (660nm)" package="0603 [SMD]"]
  Power_LED = smd LED [color="Green (570nm)" package="0603 [SMD]"]
  J1 = Piezo Speaker
  J2 = Piezo Speaker
  J3 = Piezo Speaker
  J4 = Piezo Speaker
  U3 = RELAY [package=relay-g5q]
  U4 = RELAY [package=relay-g5q]
  V1 = AC Power [voltage=12V frequency=60Hz]
  V2 = AC Power [voltage=12V frequency=60Hz]
  Bulb = LEDs [package=led10mm]
  Bulb_2 = LEDs [package=led10mm]
  J5 = Basic Servo
  J6 = Basic Servo
  VCC_18V = Battery block 9V
  VCC2 = Battery block 9V

nets:
  N1: 4x4_Matrix_Keypad.col1, Safehouse_SoC.pin28
  N2: 4x4_Matrix_Keypad.col2, Safehouse_SoC.pin27
  N3: 4x4_Matrix_Keypad.col3, Safehouse_SoC.pin26
  N4: 4x4_Matrix_Keypad.col4, Safehouse_SoC.pin25
  N5: 4x4_Matrix_Keypad.row1, Safehouse_SoC.pin24
  N6: 4x4_Matrix_Keypad.row2, Safehouse_SoC.pin23
  N7: 4x4_Matrix_Keypad.row3, Safehouse_SoC.pin22
  N8: 4x4_Matrix_Keypad.row4, Safehouse_SoC.pin21
  N9: S2.Pin_1, S2.Pin_2, R1.Pin_0, Safehouse_SoC.pin18, Flame_Sensor.pin3, Gas_Sensor.H2
  N10: S2.Pin_3, Safehouse_SoC.pin17
  N11: S3.Pin_1, Safehouse_SoC.pin32
  N12: S3.Pin_3, S3.Pin_4, R2.Pin_1, Safehouse_SoC.pin31, PIR1.VDD
  GND: R1.Pin_1, R2.Pin_0, PIR1.GND, Flame_Sensor.pin2, Gas_Sensor.H1, LED2.cathode, LED3.cathode, LEDs.cathode, LED5.cathode, Power_LED.cathode, J1.pin1, J2.pin1, J3.pin1, J4.pin1, U3.COIL1, U4.COIL1, J5.gnd, J6.gnd
  N13: Safehouse_SoC.pin1, VCC_18V.+
  N14: Safehouse_SoC.pin2, J6.pulse
  N15: Safehouse_SoC.pin3, J5.pulse
  N16: Safehouse_SoC.pin5, U4.COIL2
  N17: Safehouse_SoC.pin6, U3.COIL2
  N18: Safehouse_SoC.pin7, J4.pin2
  N19: Safehouse_SoC.pin8, J3.pin2
  N20: Safehouse_SoC.pin9, J2.pin2
  N21: Safehouse_SoC.pin10, J1.pin2
  N22: Safehouse_SoC.pin11, LEDs.anode
  N23: Safehouse_SoC.pin12, LED3.anode
  N24: Safehouse_SoC.pin13, LED2.anode
  N25: Safehouse_SoC.pin14, LED5.anode
  N26: Safehouse_SoC.pin15, Power_LED.anode
  N27: Safehouse_SoC.pin16, VCC2.-
  N28: Safehouse_SoC.pin19, Gas_Sensor.B1
  N29: Safehouse_SoC.pin20, Flame_Sensor.pin4
  N30: Safehouse_SoC.pin30, PIR1.SIG
  N31: U3.NO, V1.V-
  N32: U3.NC, Bulb.C
  N33: U4.NO, V2.V-
  N34: U4.NC, Bulb_2.C
  N35: V1.V+, Bulb.A
  N36: V2.V+, Bulb_2.A
  5V: J5.vcc, J6.vcc
  N37: VCC_18V.-, VCC2.+

notes:
  FPGA Based SAFEHOUSE, PANKAJ KUMAR                                                                                                               03976802814                                    [ ECE-3 ], 1.0

custom parts:
  KEYPAD 4x4: Matrix keypad 16 buttons, 4 rows x 4 columns
  KY-026: ky-026 flame sensor module
  LEDs: LEDs Standard schematic elements and footprints for 5mm, 3mm, 1206, and 0603 sized LEDs. 5mm - Spark Fun Electronics SKU : COM-00529 (and others)
